// Logisim project Milestone 2 final ish.circ as structural Verilog: 3 circuits, main circuit ALU
module main (
  input  in_1,
  input  in_2,
  input  in_3,
  input  LD_SC,
  input  INR_SC,
  input  [3:0] INPUT_SC,
  output out_7,
  output out_8
);

  wire clock_1_out, control_unit_1_inr_pc, control_unit_1_ld_ac, control_unit_1_ld_ar, control_unit_1_ld_dr,
       control_unit_1_ld_ir, control_unit_1_ld_pc, control_unit_1_mem_read, control_unit_1_mem_write;
  wire [2:0] control_unit_1_alu, control_unit_1_bus_controls;
  wire [11:0] AR_q, bit_extender_1_out;
  wire [15:0] AC_q, alu_1_alu_output, bit_extender_2_out, DR_q, IR_q, multiplexer_1_out, PC_q, ram_1_data,
       TR_q;

  Clock clock_1 (.out(clock_1_out));
  Register #(.width(16)) IR (
    .D(multiplexer_1_out), .en(control_unit_1_ld_ir), .Q(IR_q), .clk(clock_1_out));  // open: clr
  Counter #(.width(16), .max('hffff)) PC (
    .load(control_unit_1_ld_pc), .D(multiplexer_1_out), .count(control_unit_1_inr_pc), .Q(PC_q),
    .clk(clock_1_out));  // open: carry, clr
  Bit_Extender #(.in_width(16), .out_width(12)) bit_extender_1 (.in(multiplexer_1_out), .out(bit_extender_1_out));
  Register #(.width(16)) AC (
    .D(alu_1_alu_output), .en(control_unit_1_ld_ac), .Q(AC_q), .clk(clock_1_out));  // open: clr
  Register #(.width(16)) DR (
    .D(multiplexer_1_out), .en(control_unit_1_ld_dr), .Q(DR_q), .clk(clock_1_out));  // open: clr
  Register #(.width(12)) AR (
    .D(bit_extender_1_out), .en(control_unit_1_ld_ar), .Q(AR_q), .clk(clock_1_out));  // open: clr
  Register #(.width(16)) TR (.D(multiplexer_1_out), .en(in_3), .Q(TR_q), .clk(clock_1_out));  // open: clr
  RAM #(.addrWidth(12), .dataWidth(16), .bus("separate")) ram_1 (
    .addr(AR_q), .din(multiplexer_1_out), .data(ram_1_data), .str(control_unit_1_mem_write),
    .clk(clock_1_out), .ld(control_unit_1_mem_read));  // open: sel, clr
  ALU alu_1 (
    .in_1(in_1), .Input_1__AC(AC_q), .Input_2__DR(DR_q), .in_4(in_2), .Selection_of_ALU(control_unit_1_alu),
    .out_6(out_7), .out_7(out_8), .ALU_Output(alu_1_alu_output));
  assign bit_extender_2_out = {{4{1'b0}}, AR_q};  // Bit_Extender bit_extender_2
  Multiplexer #(.select(3), .width(16)) multiplexer_1 (
    .in0(AC_q), .in1(DR_q), .in2(TR_q), .in3(bit_extender_2_out), .in4(ram_1_data), .in5(PC_q), .in6(IR_q),
    .out(multiplexer_1_out), .sel(control_unit_1_bus_controls));  // open: in7, en
  Control_Unit control_unit_1 (
    .IR(IR_q), .LD_SC(LD_SC), .INPUT_SC(INPUT_SC), .INR_SC(INR_SC), .CLK(clock_1_out),
    .LD_DR(control_unit_1_ld_dr), .LD_IR(control_unit_1_ld_ir), .LD_AR(control_unit_1_ld_ar),
    .BUS_CONTROLS(control_unit_1_bus_controls), .LD_AC(control_unit_1_ld_ac), .LD_PC(control_unit_1_ld_pc),
    .INR_PC(control_unit_1_inr_pc), .MEM_WRITE(control_unit_1_mem_write), .MEM_READ(control_unit_1_mem_read),
    .ALU(control_unit_1_alu));
endmodule

module ALU (
  input  in_1,
  input  [15:0] Input_1__AC,
  input  [15:0] Input_2__DR,
  input  in_4,
  input  [2:0] Selection_of_ALU,
  output out_6,
  output out_7,
  output [15:0] ALU_Output
);

  wire [15:0] adder_1_out, and_1_out, Complement_AC__DR_is_also_correct_out, or_1_out, subtractor_1_out,
       xor_1_out;

  Adder #(.width(16)) adder_1 (.a(Input_1__AC), .b(Input_2__DR), .out(adder_1_out), .cin(in_1), .cout(out_6));
  Subtractor #(.width(16)) subtractor_1 (
    .a(Input_1__AC), .b(Input_2__DR), .out(subtractor_1_out), .bin(in_4), .bout(out_7));
  assign and_1_out = Input_1__AC & Input_2__DR;  // AND_Gate and_1, 16 bits wide
  assign or_1_out = Input_1__AC | Input_2__DR;  // OR_Gate or_1, 16 bits wide
  assign xor_1_out = Input_1__AC ^ Input_2__DR;  // XOR_Gate xor_1, 16 bits wide
  assign Complement_AC__DR_is_also_correct_out = ~Input_1__AC;  // NOT_Gate Complement_AC__DR_is_also_correct, 16 bits wide
  Multiplexer #(.select(3), .width(16)) multiplexer_1 (
    .in0(adder_1_out), .in1(subtractor_1_out), .in2(Input_2__DR), .in3(and_1_out), .in4(or_1_out),
    .in5(xor_1_out), .in6(Complement_AC__DR_is_also_correct_out), .out(ALU_Output), .sel(Selection_of_ALU));  // open: in7, en
endmodule

module Control_Unit (
  input  [15:0] IR,
  input  LD_SC,
  input  [3:0] INPUT_SC,
  input  INR_SC,
  input  CLK,
  output LD_DR,
  output LD_IR,
  output LD_AR,
  output [2:0] BUS_CONTROLS,
  output LD_AC,
  output LD_PC,
  output INR_PC,
  output MEM_WRITE,
  output MEM_READ,
  output [2:0] ALU
);

  wire and_3_out, and_10_out, and_11_out, D_FF_q, decoder_1_out0, decoder_1_out1, decoder_1_out2,
       decoder_1_out4, decoder_1_out7, decoder_2_out3, decoder_2_out4, decoder_2_out5, I_qn;
  wire [2:0] bitselector_1_out;
  wire [3:0] SC_q;

  D_Flip_Flop D_FF (.clk(CLK), .D(LD_AC), .Q(D_FF_q));  // open: Qn, preset, en, reset
  D_Flip_Flop I (.clk(CLK), .D(IR[15]), .Qn(I_qn));  // open: Q, preset, en, reset
  Counter #(.width(4), .max('hf)) SC (
    .load(LD_SC), .D(INPUT_SC), .count(INR_SC), .Q(SC_q), .clk(D_FF_q), .clr(D_FF_q));  // open: carry
  Decoder #(.select(3), .enable("false")) decoder_1 (
    .out0(decoder_1_out0), .out1(decoder_1_out1), .out2(decoder_1_out2), .out3(decoder_1_out1),
    .out4(decoder_1_out4), .out7(decoder_1_out7), .sel(IR[14:12]));  // open: out5, out6
  Decoder #(.select(4), .enable("false")) decoder_2 (
    .out0(LD_AR), .out1(LD_IR), .out3(decoder_2_out3), .out4(decoder_2_out4), .out5(decoder_2_out5),
    .sel(SC_q));  // open: out2, out6, out7, out8, out9, out10, out11, out12, out13, out14, out15
  BitSelector #(.width(1), .group(3)) bitselector_1 (.in(LD_AC), .out(bitselector_1_out));  // open: sel
  and and_1 (LD_AC, decoder_1_out1, decoder_2_out4);
  and and_2 (LD_AC, decoder_1_out4, decoder_2_out4);
  and and_3 (and_3_out, decoder_1_out7, IR[2], I_qn, decoder_2_out3);
  Multiplexer #(.select(3), .width(3), .enable("false")) multiplexer_1 (
    .in1(bitselector_1_out), .in2({3{LD_AC}}), .in4({3{LD_AC}}), .out(ALU), .sel({3{LD_AC}}));  // open: in0, in3, in5, in6, in7
  and and_4 (LD_AC, decoder_1_out0, decoder_2_out5);
  and and_5 (LD_DR, decoder_1_out1, decoder_2_out4);
  and and_6 (LD_DR, decoder_1_out2, decoder_2_out4);
  and and_7 (LD_AC, decoder_1_out1, decoder_2_out5);
  and and_8 (LD_AC, decoder_1_out2, decoder_2_out5);
  and and_9 (LD_DR, decoder_1_out0, decoder_2_out4);
  and and_10 (and_10_out, decoder_1_out2, decoder_2_out5);
  and and_11 (and_11_out, decoder_1_out4, decoder_2_out4);
  or or_1 (INR_PC, LD_IR, and_3_out);
  and and_12 (BUS_CONTROLS[2], decoder_1_out1, decoder_2_out4);
  or or_2 (MEM_READ, LD_IR, LD_DR);
  or or_3 (BUS_CONTROLS[0], and_10_out, and_11_out);
  or or_4 (BUS_CONTROLS[1], and_10_out, LD_AR);

  assign LD_PC = LD_AC;
  assign MEM_WRITE = LD_AC;

  // Notes on the sheet:
  //   Transfer
  //   AND
  //   Add
  //   BUS DR 
  //   BUS AR
  //   BUS AC
endmodule
