// Logisim project Registers.circ as structural Verilog: 3 circuits, main circuit main
module main (
  input  [2:0] C2C1C0,
  input  Load,
  input  Load_2,
  input  Clear,
  input  Clear_2,
  input  [2:0] S2S1S0,
  input  Enable,
  input  Clear_3,
  input  Clear_4,
  input  Load_3,
  input  WRITE,
  input  Load_4,
  input  READ,
  input  Clear_5,
  output E
);

  wire clock_1_out, undriven;
  wire [5:0] AR_q, bit_extender_1_out;
  wire [15:0] AC_q, ALU_out_ac, bit_extender_2_out, bus_1_busout, DR_q, ram_1_data, TR_q;

  Bit_Extender #(.in_width(16), .out_width(6)) bit_extender_1 (.in(bus_1_busout), .out(bit_extender_1_out));
  ALU ALU (.DR(DR_q), .AC(AC_q), .C2C1C0(C2C1C0), .E(E), .OUT_AC(ALU_out_ac));
  Register #(.width(6)) AR (.D(bit_extender_1_out), .en(Load_4), .Q(AR_q), .clk(clock_1_out), .clr(Clear_5));
  Register #(.width(16)) AC (.D(ALU_out_ac), .en(Load), .Q(AC_q), .clk(clock_1_out), .clr(Clear));
  Register #(.width(16)) DR (.D(bus_1_busout), .en(Load_2), .Q(DR_q), .clk(clock_1_out), .clr(Clear_2));
  Register #(.width(16)) TR (.D(bus_1_busout), .Q(TR_q), .clk(clock_1_out), .clr(Clear_3));  // open: en
  RAM #(.addrWidth(6), .dataWidth(16), .bus("separate")) ram_1 (
    .addr(AR_q), .din(bus_1_busout), .data(ram_1_data), .str(WRITE), .sel(undriven), .clk(clock_1_out),
    .ld(READ), .clr(Clear_4));
  Clock clock_1 (.out(clock_1_out));
  assign bit_extender_2_out = {{10{1'b0}}, AR_q};  // Bit_Extender bit_extender_2
  BUS bus_1 (
    .AC(AC_q), .DR(DR_q), .TR(TR_q), .AR(bit_extender_2_out), .RAM(ram_1_data), .S2S1S0(S2S1S0), .E(Enable),
    .BUSOUT(bus_1_busout));
endmodule

module ALU (
  input  [15:0] DR,
  input  [15:0] AC,
  input  [2:0] C2C1C0,
  output E,
  output [15:0] OUT_AC
);

  wire [15:0] adder_1_out, and_1_out, not_1_out, or_1_out, subtractor_1_out, xor_1_out;

  Adder #(.width(16)) adder_1 (.a(AC), .b(AC), .out(adder_1_out), .cout(E));  // open: cin
  Subtractor #(.width(16)) subtractor_1 (.a(AC), .b(AC), .out(subtractor_1_out));  // open: bin, bout
  assign and_1_out = AC & AC;  // AND_Gate and_1, 16 bits wide
  assign or_1_out = AC | AC;  // OR_Gate or_1, 16 bits wide
  assign xor_1_out = AC ^ AC;  // XOR_Gate xor_1, 16 bits wide
  assign not_1_out = ~AC;  // NOT_Gate not_1, 16 bits wide
  Multiplexer #(.select(3), .width(16), .enable("false")) multiplexer_1 (
    .in0(adder_1_out), .in1(subtractor_1_out), .in2(AC), .in3(and_1_out), .in4(or_1_out), .in5(xor_1_out),
    .in6(not_1_out), .out(OUT_AC), .sel(C2C1C0));  // open: in7

  assign DR = AC;
endmodule

module BUS (
  input  [15:0] AC,
  input  [15:0] DR,
  input  [15:0] TR,
  input  [15:0] AR,
  input  [15:0] RAM,
  input  [2:0] S2S1S0,
  input  E,
  output [15:0] BUSOUT
);

  Multiplexer #(.select(3)) multiplexer_1 (
    .in0(AC[3]), .in1(DR[3]), .in2(TR[3]), .in3(AR[3]), .in4(RAM[3]), .out(BUSOUT[3]), .sel(S2S1S0), .en(E));  // open: in5, in6, in7
  Multiplexer #(.select(3)) multiplexer_2 (
    .in0(AC[4]), .in1(DR[4]), .in2(TR[4]), .in3(AR[4]), .in4(RAM[4]), .out(BUSOUT[4]), .sel(S2S1S0), .en(E));  // open: in5, in6, in7
  Multiplexer #(.select(3)) multiplexer_3 (
    .in0(AC[5]), .in1(DR[5]), .in2(TR[5]), .in3(AR[5]), .in4(RAM[5]), .out(BUSOUT[5]), .sel(S2S1S0), .en(E));  // open: in5, in6, in7
  Multiplexer #(.select(3)) multiplexer_4 (
    .in0(AC[6]), .in1(DR[6]), .in2(TR[6]), .in3(AR[6]), .in4(RAM[6]), .out(BUSOUT[6]), .sel(S2S1S0), .en(E));  // open: in5, in6, in7
  Multiplexer #(.select(3)) multiplexer_5 (
    .in0(AC[7]), .in1(DR[7]), .in2(TR[7]), .in3(AR[7]), .in4(RAM[7]), .out(BUSOUT[7]), .sel(S2S1S0), .en(E));  // open: in5, in6, in7
  Multiplexer #(.select(3)) multiplexer_6 (
    .in0(AC[9]), .in1(DR[9]), .in2(TR[9]), .in3(AR[9]), .in4(RAM[9]), .out(BUSOUT[9]), .sel(S2S1S0), .en(E));  // open: in5, in6, in7
  Multiplexer #(.select(3)) multiplexer_7 (
    .in0(AC[10]), .in1(DR[10]), .in2(TR[10]), .in3(AR[10]), .in4(RAM[10]), .out(BUSOUT[10]), .sel(S2S1S0),
    .en(E));  // open: in5, in6, in7
  Multiplexer #(.select(3)) multiplexer_8 (
    .in0(AC[11]), .in1(DR[11]), .in2(TR[11]), .in3(AR[11]), .in4(RAM[11]), .out(BUSOUT[11]), .sel(S2S1S0),
    .en(E));  // open: in5, in6, in7
  Multiplexer #(.select(3)) multiplexer_9 (
    .in0(AC[15]), .in1(DR[15]), .in2(TR[15]), .in3(AR[15]), .in4(RAM[15]), .out(BUSOUT[15]), .sel(S2S1S0),
    .en(E));  // open: in5, in6, in7
  Multiplexer #(.select(3)) multiplexer_10 (
    .in0(AC[8]), .in1(DR[8]), .in2(TR[8]), .in3(AR[8]), .in4(RAM[8]), .out(BUSOUT[8]), .sel(S2S1S0), .en(E));  // open: in5, in6, in7
  Multiplexer #(.select(3)) multiplexer_11 (
    .in0(AC[12]), .in1(DR[12]), .in2(TR[12]), .in3(AR[12]), .in4(RAM[12]), .out(BUSOUT[12]), .sel(S2S1S0),
    .en(E));  // open: in5, in6, in7
  Multiplexer #(.select(3)) multiplexer_12 (
    .in0(AC[13]), .in1(DR[13]), .in2(TR[13]), .in3(AR[13]), .in4(RAM[13]), .out(BUSOUT[13]), .sel(S2S1S0),
    .en(E));  // open: in5, in6, in7
  Multiplexer #(.select(3)) multiplexer_13 (
    .in0(AC[14]), .in1(DR[14]), .in2(TR[14]), .in3(AR[14]), .in4(RAM[14]), .out(BUSOUT[14]), .sel(S2S1S0),
    .en(E));  // open: in5, in6, in7
  Multiplexer #(.select(3)) multiplexer_14 (
    .in0(AC[0]), .in1(DR[0]), .in2(TR[0]), .in3(AR[0]), .in4(RAM[0]), .out(BUSOUT[0]), .sel(S2S1S0), .en(E));  // open: in5, in6, in7
  Multiplexer #(.select(3)) multiplexer_15 (
    .in0(AC[1]), .in1(DR[1]), .in2(TR[1]), .in3(AR[1]), .in4(RAM[1]), .out(BUSOUT[1]), .sel(S2S1S0), .en(E));  // open: in5, in6, in7
  Multiplexer #(.select(3)) multiplexer_16 (
    .in0(AC[2]), .in1(DR[2]), .in2(TR[2]), .in3(AR[2]), .in4(RAM[2]), .out(BUSOUT[2]), .sel(S2S1S0), .en(E));  // open: in5, in6, in7
endmodule
